# Fritzing sketch circuit (saved by Fritzing 0.9.3b)
breadboards: 1

parts:
  U1 = NodeMCU V3.0
  U3 = POT [package=trim_pot]
  R1 = Resistor [tolerance=±5% resistance=330 package="0805 [SMD]"]
  R5 = Resistor [tolerance=±5% resistance=220 package="2512 [SMD]"]
  Part1 = SHT1x-Breakout  # not connected
  LED1 = LED - 3mm [color="Red (633nm)" package="3 mm [THT]"]

nets:
  N1: U1.GND#6, U1.GND#13, U1.GND#16, U1.GND#33
  N2: U1.A0, R1.Pin_0
  N3: U3.S, R5.Pin_0
  N4: U3.E, R1.Pin_1
  N5: U3.A, LED1.cathode
  N6: R5.Pin_1, LED1.anode

custom parts:
  NodeMCU V3.0: ESP8266 based NodeMCU
